# Fritzing sketch sketch (saved by Fritzing 0.9.3b)
circuit board: 8.46667cm x 5.64444cm
breadboards: 1

parts:
  S1 = Tactile Switch Buttons - 12mm Square [package=tactile-pth-12mm]
  S2 = Tactile Switch Buttons - 12mm Square [package=tactile-pth-12mm]
  S3 = Tactile Switch Buttons - 12mm Square [package=tactile-pth-12mm]
  S4 = Tactile Switch Buttons - 12mm Square [package=tactile-pth-12mm]
  R1 = Resistor [tolerance=±5% resistance=1k package="0603 [SMD]"]
  R2 = Resistor [tolerance=±5% resistance=1k package="0603 [SMD]"]
  R3 = Resistor [tolerance=±5% resistance=1k package="0603 [SMD]"]
  R4 = Resistor [tolerance=±5% resistance=1k package="0603 [SMD]"]
  Raspberry_Pi_1 = Raspberry Pi 3 [part_number=RPI-3-V1.2]

nets:
  N1: S1.1, S1.3, Raspberry_Pi_1.GPIO26
  N2: S2.1, Raspberry_Pi_1.GPIO19
  N3: S3.1, Raspberry_Pi_1.GPIO13
  N4: S4.1, Raspberry_Pi_1.GPIO6
  N5: R1.Pin_1, R2.Pin_1, R3.Pin_1, R4.Pin_1, Raspberry_Pi_1.5V

custom parts:
  Tactile Switch Buttons - 12mm Square: Medium-sized clicky momentary switches are standard input "buttons" on electronic projects. These work best in a PCB but can be used on a solderless breadboard as shown in this tutorial. The pins are normally open (disconnected) and when the button is pressed they are momentarily closed. They come in a pack of 10, they're pretty handy so you'll want to keep them around. You can find an EAGLE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
